# Fritzing sketch BatteryLEDCombo (saved by Fritzing 1.0.5)

parts:
  U3 = ESP32-38PinWide [part_number=ESP32-38PinWide]
  A2 = TJA1050 CAN Module
  cntl1 = roboRIO
  Mod1 = VRM
  U4 = RFID RC522 SIP - 8 pins [chip_label="RFID RC522" package="SIP (Single Inline) [THT]"]
  U5 = RFID RC522 SIP - 8 pins [chip_label="RFID RC522" package="SIP (Single Inline) [THT]"]
  PDP1 = PDP
  U6 = WS2812 RGB LED strip

nets:
  VCC: U3.3.3, U4.VCC, U5.VCC
  N1: U3.GPIO32, U5.NSS
  N2: U3.GPIO33, U4.IRQ
  GND: U3.GND, A2.Pin_2, cntl1.DIO0_GND, cntl1.Power_GND, cntl1.Pin_16, cntl1.RY1_GND, cntl1.IN_A2_GND, Mod1.5V_2A_GND0, Mod1.InGnd, U4.GND, U5.GND, PDP1.4_+, PDP1.VRM_PCM_0-, PDP1.CONT_-
  N3: U3.VIN, A2.Pin_3, Mod1.5V_2A_5V0
  N4: U3.GPIO4, A2.Pin_1
  N5: U3.GPIO16, U6.DIN
  N6: U3.GPIO5, A2.Pin_4
  N7: U3.GPIO18, U4.SCK, U5.SCK
  N8: U3.GPIO19, U4.MISO, U5.MISO
  N9: U3.GPIO22, U4.RST, U5.RST
  N10: U3.GPIO23, U4.MOSI, U5.MOSI
  N11: A2.Pin_5, cntl1.CAN_L_(GRN), PDP1.CAN_G_1
  N12: A2.Pin_6, cntl1.CAN_H_(YEL), PDP1.CAN_Y_1
  N13: cntl1.Power_+VIN, PDP1.CONT_+
  N14: Mod1.In12V, PDP1.VRM_PCM_0+

notes:
  CTRE PDP or REV PDH is reqauired for energy monitoring.
  Your RC522 might look different. Always check label!
  Reader 1 SS GPIO 32
  Reader 2 SS GPIO 33
  CAN TX Transmit Line GPIO 4 Connected to CAN transceiver TX
  CAN RX Receive Line GPIO 5 Connected to CAN transceiver RX
  Your Transceiver will have a different pinout so DOUBLE CHECK!
  IO16 -> LED Din
  Power you LED based on it's voltage

custom parts:
  ESP32-38PinWide: Generic 38-Pin ESP32 with wide format (only access to one side of pins on a breadboard) based on Stephen Lilley's HiLetgo ESP-WROOM-32 ESP32 ESP-32S Development Board.
  TJA1050 CAN Module: TJA1050 CAN module CAN bus module.
  RFID RC522 SIP - 8 pins: A SIP stand-in part for RFID RC522 . With 8 pins on a 300 mil single inline package (SIP) footprint.
  WS2812 RGB LED strip: WS2812 strip
