# Fritzing sketch BatteryRFIDLF (saved by Fritzing 1.0.5)

parts:
  U3 = ESP32-38PinWide [part_number=ESP32-38PinWide]
  A2 = TJA1050 CAN Module
  cntl1 = roboRIO
  Mod1 = VRM
  125_kHz_RFID_module1 = RDM6300
  Part1 = RDM6300-ANT

nets:
  GND: U3.GPIO26, U3.GND, A2.Pin_2, Mod1.5V_2A_GND0, Mod1.12V_2A_GND0, Mod1.InGnd, 125_kHz_RFID_module1.TX, 125_kHz_RFID_module1.GND
  VIN: U3.VIN, A2.Pin_3, Mod1.5V_2A_5V0, 125_kHz_RFID_module1.+5V
  N1: U3.GPIO4, A2.Pin_1
  N2: U3.GPIO5, A2.Pin_4
  N3: A2.Pin_5, cntl1.CAN_L_(GRN)
  N4: A2.Pin_6, cntl1.CAN_H_(YEL)
  N5: 125_kHz_RFID_module1.ANT1, Part1.ANT1
  N6: 125_kHz_RFID_module1.ANT2, Part1.ANT2

notes:
  CAN_TX_PIN GPIO 4
  CAN_RX_PIN GPIO 5
  Check your module for the exact pinout.
  You needs to go TX to TX, RX to RX for CAN transceiver
  Only TX from reader is needed to ESP32 GPIO 26

custom parts:
  ESP32-38PinWide: Generic 38-Pin ESP32 with wide format (only access to one side of pins on a breadboard) based on Stephen Lilley's HiLetgo ESP-WROOM-32 ESP32 ESP-32S Development Board.
  TJA1050 CAN Module: TJA1050 CAN module CAN bus module.
  RDM6300: 125 kHz RFID module (serial interface)
  RDM6300-ANT: Antenna
