# Fritzing sketch addressableLED (saved by Fritzing 1.0.5)

parts:
  U1 = ESP32-38PinWide [part_number=ESP32-38PinWide]
  A1 = TJA1050 CAN Module
  cntl1 = roboRIO
  U2 = WS2812 RGB LED strip
  C1 = Capacitor Polarized [package=cpol-radial-10uf-25v]
  Mod1 = VRM

nets:
  GND: U1.GND, A1.Pin_2, U2.GND, C1.-, Mod1.5V_2A_GND0, Mod1.InGnd
  VIN: U1.VIN, A1.Pin_3, U2.VCC, C1.+, Mod1.5V_2A_5V0
  N1: U1.GPIO4, A1.Pin_1
  N2: U1.GPIO16, U2.DIN
  N3: U1.GPIO5, A1.Pin_4
  N4: A1.Pin_5, cntl1.CAN_L_(GRN)
  N5: A1.Pin_6, cntl1.CAN_H_(YEL)

custom parts:
  ESP32-38PinWide: Generic 38-Pin ESP32 with wide format (only access to one side of pins on a breadboard) based on Stephen Lilley's HiLetgo ESP-WROOM-32 ESP32 ESP-32S Development Board.
  TJA1050 CAN Module: TJA1050 CAN module CAN bus module.
  WS2812 RGB LED strip: WS2812 strip
