# Fritzing sketch minimum (saved by Fritzing 1.0.5)

parts:
  U1 = ESP32-38PinWide [part_number=ESP32-38PinWide]
  A1 = TJA1050 CAN Module
  cntl1 = roboRIO
  Mod1 = VRM
  U2 = ESP32-38PinWide [part_number=ESP32-38PinWide]
  A2 = TJA1050 CAN Module
  Mod1_2 = VRM
  ctrl1 = rev_spark_max [part_number=rev-11-2158]
  BLDC1 = CTRE Falcon 500 [part_number=19-708850]
  PDP1 = PDP

nets:
  N1: U1.GND, A1.Pin_2, Mod1.5V_2A_GND0, Mod1.InGnd
  N2: U1.VIN, A1.Pin_3, Mod1.5V_2A_5V0
  N3: U1.GPIO4, A1.Pin_1
  N4: U1.GPIO5, A1.Pin_4
  N5: A1.Pin_5, cntl1.CAN_L_(GRN), A2.Pin_5, ctrl1.connector7
  N6: A1.Pin_6, cntl1.CAN_H_(YEL), A2.Pin_6, ctrl1.connector6
  N7: U2.GND, A2.Pin_2, Mod1_2.5V_2A_GND0, Mod1_2.InGnd
  N8: U2.VIN, A2.Pin_3, Mod1_2.5V_2A_5V0
  N9: U2.GPIO4, A2.Pin_1
  N10: U2.GPIO5, A2.Pin_4
  N11: ctrl1.connector4, BLDC1.CANH1#3
  N12: ctrl1.connector5, BLDC1.CANL0
  N13: BLDC1.CANL1, PDP1.CAN_G_0
  N14: BLDC1.CANH1#5, PDP1.CAN_Y_0

notes:
  Graphic based on https://github.com/AronRubin/FRCFritzingParts
  CAN Terminated at PDP

custom parts:
  ESP32-38PinWide: Generic 38-Pin ESP32 with wide format (only access to one side of pins on a breadboard) based on Stephen Lilley's HiLetgo ESP-WROOM-32 ESP32 ESP-32S Development Board.
  TJA1050 CAN Module: TJA1050 CAN module CAN bus module.
  CTRE Falcon 500: The Falcon 500 powered by Talon FX is a brushless motor with an integrated motor controller and high-resolution encoder, custom designed specifically for the FIRST Robotics Competition, through a collaboration between Cross the Road Electronics and VEX Robotics.
